# Fritzing sketch schematic (saved by Fritzing 0.9.3b)
breadboards: 1

parts:
  Part1 = Photon
  Q1 = TRANSISTOR_PNP [part_number=2N3906 package=to-92]
  Q2 = NPN-Transistor [part_number=2N3904 package="TO92 [THT]"]
  R1 = Resistor [tolerance=±5% resistance=10k package=THT]
  R2 = Resistor [tolerance=±5% resistance=10k package=THT]
  Q3 = TRANSISTOR_PNP [part_number=2N3906 package=to-92]
  Q4 = NPN-Transistor [part_number=2N3904 package="TO92 [THT]"]
  R3 = Resistor [tolerance=±5% resistance=10k package=THT]
  R4 = Resistor [tolerance=±5% resistance=10k package=THT]
  Q5 = TRANSISTOR_PNP [part_number=2N3906 package=to-92]
  Q6 = NPN-Transistor [part_number=2N3904 package="TO92 [THT]"]
  R5 = Resistor [tolerance=±5% resistance=10k package=THT]
  R6 = Resistor [tolerance=±5% resistance=10k package=THT]
  C1 = Ceramic Capacitor [capacitance=100nF package="100 mil [THT, multilayer]"]
  S1 = Pushbutton [package="[THT]"]
  C2 = Ceramic Capacitor [capacitance=100nF package="100 mil [THT, multilayer]"]
  S2 = Pushbutton [package="[THT]"]

nets:
  N1: Part1.D0, R1.Pin_0
  N2: Part1.D1, R3.Pin_0
  N3: Part1.D2, R5.Pin_0
  N4: Part1.D5, C1.0, S1.Pin_3, S1.Pin_4
  N5: Part1.D6, C2.0, S2.Pin_4
  5V: Q1.E, Q3.E, Q5.E
  N6: Q1.B, R2.Pin_1
  GND: Q2.E, Q4.E, Q6.E, C1.1, C2.1
  N7: Q2.B, R1.Pin_1
  N8: Q2.C, R2.Pin_0
  N9: Q3.B, R4.Pin_1
  N10: Q4.B, R3.Pin_1
  N11: Q4.C, R4.Pin_0
  N12: Q5.B, R6.Pin_1
  N13: Q6.B, R5.Pin_1
  N14: Q6.C, R6.Pin_0

notes:
  to led strip 5V+
  to bright white led 5V+
